# Fritzing sketch Platine IO Arduino Mega (saved by Fritzing 0.9.3b)
circuit board: 12.9cm x 6cm
breadboards: 3

parts:
  J8 = male pin header, 18 pins [form="♂ (male)"]
  J7 = male pin header, 8 pins [form="♂ (male)"]
  J6 = male pin header, 8 pins [form="♂ (male)"]
  J5 = male pin header, 8 pins [form="♂ (male)"]  # not connected
  J3 = male pin header, 8 pins [form="♂ (male)"]
  J4 = male pin header, 8 pins [form="♂ (male)"]
  R1 = Resistor [tolerance=±5% resistance=10k package=THT]
  J10 = female pin header, 8 pins [form="♀ (female)"]
  J11 = female pin header, 8 pins [form="♀ (female)"]
  J12 = female pin header, 8 pins [form="♀ (female)"]
  J14 = female pin header, 8 pins [form="♀ (female)"]
  R2 = Resistor [tolerance=±5% resistance=10k package=THT]
  R3 = Resistor [tolerance=±5% resistance=10k package=THT]
  R4 = Resistor [tolerance=±5% resistance=10k package=THT]
  R5 = Resistor [tolerance=±5% resistance=10k package=THT]
  R6 = Resistor [tolerance=±5% resistance=10k package=THT]
  R7 = Resistor [tolerance=±5% resistance=10k package=THT]
  R8 = Resistor [tolerance=±5% resistance=10k package=THT]
  R9 = Resistor [tolerance=±5% resistance=10k package=THT]
  R10 = Resistor [tolerance=±5% resistance=10k package=THT]
  R11 = Resistor [tolerance=±5% resistance=10k package=THT]
  R12 = Resistor [tolerance=±5% resistance=10k package=THT]
  R13 = Resistor [tolerance=±5% resistance=10k package=THT]
  J15 = female pin header, 8 pins [form="♀ (female)"]
  J2 = male pin header, 10 pins [form="♂ (male)"]
  R14 = Resistor [tolerance=±5% resistance=10k package=THT]
  R15 = Resistor [tolerance=±5% resistance=10k package=THT]
  R16 = Resistor [tolerance=±5% resistance=10k package=THT]
  J19 = male pin header, 2 pins [form="♂ (male)"]
  J20 = male pin header, 12 pins [form="♂ (male)"]
  IC1 = ULN2803A [package=THT]
  IC2 = ULN2803A [package=THT]
  R17 = Resistor [tolerance=±5% resistance=330 package=THT]
  R18 = Resistor [tolerance=±5% resistance=330 package=THT]
  R19 = Resistor [tolerance=±5% resistance=330 package=THT]
  R20 = Resistor [tolerance=±5% resistance=330 package=THT]
  R21 = Resistor [tolerance=±5% resistance=330 package=THT]
  R22 = Resistor [tolerance=±5% resistance=330 package=THT]
  R23 = Resistor [tolerance=±5% resistance=330 package=THT]
  R24 = Resistor [tolerance=±5% resistance=330 package=THT]
  R25 = Resistor [tolerance=±5% resistance=330 package=THT]
  R26 = Resistor [tolerance=±5% resistance=330 package=THT]
  R27 = Resistor [tolerance=±5% resistance=330 package=THT]
  R28 = Resistor [tolerance=±5% resistance=330 package=THT]
  R29 = Resistor [tolerance=±5% resistance=330 package=THT]
  R30 = Resistor [tolerance=±5% resistance=330 package=THT]
  R31 = Resistor [tolerance=±5% resistance=330 package=THT]
  R32 = Resistor [tolerance=±5% resistance=330 package=THT]
  Q1 = female pin header, 2 pins [form="♀ (female)"]
  Q2 = female pin header, 2 pins [form="♀ (female)"]
  Q3 = female pin header, 2 pins [form="♀ (female)"]
  Q4 = female pin header, 2 pins [form="♀ (female)"]
  Q5 = female pin header, 2 pins [form="♀ (female)"]
  Q6 = female pin header, 2 pins [form="♀ (female)"]
  Q7 = female pin header, 2 pins [form="♀ (female)"]
  Q8 = female pin header, 2 pins [form="♀ (female)"]
  Q16 = female pin header, 2 pins [form="♀ (female)"]
  Q9 = female pin header, 2 pins [form="♀ (female)"]
  Q10 = female pin header, 2 pins [form="♀ (female)"]
  Q11 = female pin header, 2 pins [form="♀ (female)"]
  Q12 = female pin header, 2 pins [form="♀ (female)"]
  Q13 = female pin header, 2 pins [form="♀ (female)"]
  Q14 = female pin header, 2 pins [form="♀ (female)"]
  Q15 = female pin header, 2 pins [form="♀ (female)"]
  JP1 = male pin header, 3 pins [form="♂ (male)"]
  J22 = Screw terminal - 2 pins [package=THT]
  J23 = Screw terminal - 2 pins [package=THT]
  J9 = male pin header, 18 pins [form="♂ (male)"]
  J24 = male pin header, 8 pins [form="♂ (male)"]
  J25 = male pin header, 8 pins [form="♂ (male)"]
  J17 = male pin header, 10 pins [form="♂ (male)"]
  J26 = male pin header, 6 pins [form="♂ (male)"]
  J27 = male pin header, 6 pins [form="♂ (male)"]
  C1 = Ceramic Capacitor [capacitance=100nF package="200 mil [THT, multilayer]"]
  I1 = Reed switch [package=THT]
  C2 = Ceramic Capacitor [capacitance=100nF package="200 mil [THT, multilayer]"]
  I2 = Reed switch [package=THT]
  C3 = Ceramic Capacitor [capacitance=100nF package="200 mil [THT, multilayer]"]
  I3 = Reed switch [package=THT]
  C4 = Ceramic Capacitor [capacitance=100nF package="200 mil [THT, multilayer]"]
  I4 = Reed switch [package=THT]
  C5 = Ceramic Capacitor [capacitance=100nF package="200 mil [THT, multilayer]"]
  I5 = Reed switch [package=THT]
  C6 = Ceramic Capacitor [capacitance=100nF package="200 mil [THT, multilayer]"]
  I6 = Reed switch [package=THT]
  C7 = Ceramic Capacitor [capacitance=100nF package="200 mil [THT, multilayer]"]
  I7 = Reed switch [package=THT]
  C8 = Ceramic Capacitor [capacitance=100nF package="200 mil [THT, multilayer]"]
  I8 = Reed switch [package=THT]
  C9 = Ceramic Capacitor [capacitance=100nF package="200 mil [THT, multilayer]"]
  I9 = Reed switch [package=THT]
  C10 = Ceramic Capacitor [capacitance=100nF package="200 mil [THT, multilayer]"]
  I10 = Reed switch [package=THT]
  C11 = Ceramic Capacitor [capacitance=100nF package="200 mil [THT, multilayer]"]
  I11 = Reed switch [package=THT]
  C12 = Ceramic Capacitor [capacitance=100nF package="200 mil [THT, multilayer]"]
  I12 = Reed switch [package=THT]
  C13 = Ceramic Capacitor [capacitance=100nF package="200 mil [THT, multilayer]"]
  I13 = Reed switch [package=THT]
  C14 = Ceramic Capacitor [capacitance=100nF package="200 mil [THT, multilayer]"]
  I14 = Reed switch [package=THT]
  C15 = Ceramic Capacitor [capacitance=100nF package="200 mil [THT, multilayer]"]
  I15 = Reed switch [package=THT]
  C16 = Ceramic Capacitor [capacitance=100nF package="200 mil [THT, multilayer]"]
  I16 = Reed switch [package=THT]
  JP2 = male pin header, 2 pins [form="♂ (male)"]
  JP3 = male pin header, 2 pins [form="♂ (male)"]

nets (from the pcb view):
  N1: J8.pin1, J3.pin6, J3.pin7, R1.Pin_1, J10.pin6, J10.pin7, J14.pin2, R2.Pin_1, R3.Pin_1, R4.Pin_1, R5.Pin_1, R6.Pin_1, R7.Pin_1, R8.Pin_1, R9.Pin_1, R10.Pin_1, R11.Pin_1, R12.Pin_1, R13.Pin_1, J2.pin4, R14.Pin_1, R15.Pin_1, R16.Pin_1, IC1.0V, IC2.0V, J22.pin2, J23.pin2, J9.pin1, J24.pin1, J24.pin2, J24.pin3, J24.pin4, J24.pin5, J24.pin6, J24.pin7, J24.pin8, J26.pin1, J26.pin2, J26.pin3, J26.pin4, J26.pin5, J26.pin6
  N2: J8.pin2, IC2.In_8
  N3: J8.pin3, IC2.In_7
  N4: J8.pin4, IC2.In_6
  N5: J8.pin5, IC2.In_5
  N6: J8.pin6, IC2.In_4
  N7: J8.pin7, IC2.In_3
  N8: J8.pin8, IC2.In_2
  N9: J8.pin9, IC2.In_1
  N10: J8.pin10, IC1.In_8
  N11: J8.pin11, IC1.In_7
  N12: J8.pin12, IC1.In_6
  N13: J8.pin13, IC1.In_5
  N14: J8.pin14, IC1.In_4
  N15: J8.pin15, IC1.In_3
  N16: J8.pin16, IC1.In_2
  N17: J8.pin17, IC1.In_1
  N18: J8.pin18, J3.pin5, J10.pin5, J9.pin18, J25.pin1, J25.pin2, J25.pin3, J25.pin4, J25.pin5, J25.pin6, J25.pin7, J25.pin8, C1.1, I1.pin_2, C2.1, I2.pin_2, C3.1, I3.pin_2, C4.1, I4.pin_2, C5.1, I5.pin_2, C6.1, I6.pin_2, C7.1, I7.pin_2, C8.1, I8.pin_2, C9.1, I9.pin_2, C10.1, I10.pin_2, C11.1, I11.pin_2, C12.1, I12.pin_2, C13.1, I13.pin_2, C14.1, I14.pin_2, C15.1, I15.pin_2, C16.1, I16.pin_2, JP2.pin1
  N19: J7.pin1, J12.pin1, J20.pin7
  N20: J7.pin2, J12.pin2, J20.pin8
  N21: J7.pin3, J12.pin3, J20.pin9
  N22: J7.pin4, J12.pin4, J20.pin10
  N23: J7.pin5, J12.pin5, J20.pin11
  N24: J7.pin6, J12.pin6, J20.pin12
  N25: J7.pin7, J12.pin7, J17.pin1
  N26: J7.pin8, J12.pin8, J17.pin2
  N27: J6.pin1, J15.pin1, J17.pin3
  N28: J6.pin2, J15.pin2, J17.pin4
  N29: J6.pin3, J15.pin3, J17.pin5
  N30: J6.pin4, J15.pin4, J17.pin6
  N31: J6.pin5, J15.pin5, J17.pin7
  N32: J6.pin6, J15.pin6, J17.pin8
  N33: J6.pin7, J15.pin7, J17.pin9
  N34: J6.pin8, J15.pin8, J17.pin10
  N35: J3.pin1, J10.pin1
  N36: J3.pin2, J10.pin2
  N37: J3.pin3, J10.pin3
  N38: J3.pin4, J10.pin4
  N39: J3.pin8, J10.pin8, JP1.pin1, J23.pin1
  N40: J4.pin1, J11.pin1
  N41: J4.pin2, J11.pin2
  N42: J4.pin3, J11.pin3
  N43: J4.pin4, J11.pin4
  N44: J4.pin5, J11.pin5
  N45: J4.pin6, J11.pin6
  N46: J4.pin7, J11.pin7
  N47: J4.pin8, J11.pin8
  N48: R1.Pin_0, J9.pin17, C1.0, I1.pin_1
  N49: J14.pin1, J2.pin3
  N50: J14.pin3, J2.pin5, J20.pin1
  N51: J14.pin4, J2.pin6, J20.pin2
  N52: J14.pin5, J2.pin7, J20.pin3
  N53: J14.pin6, J2.pin8, J20.pin4
  N54: J14.pin7, J2.pin9, J20.pin5
  N55: J14.pin8, J2.pin10, J20.pin6
  N56: R2.Pin_0, J9.pin16, C2.0, I2.pin_1
  N57: R3.Pin_0, J9.pin15, C3.0, I3.pin_1
  N58: R4.Pin_0, J9.pin14, C4.0, I4.pin_1
  N59: R5.Pin_0, J9.pin13, C5.0, I5.pin_1
  N60: R6.Pin_0, J9.pin12, C6.0, I6.pin_1
  N61: R7.Pin_0, J9.pin11, C7.0, I7.pin_1
  N62: R8.Pin_0, J9.pin10, C8.0, I8.pin_1
  N63: R9.Pin_0, J9.pin9, C9.0, I9.pin_1
  N64: R10.Pin_0, J9.pin8, C10.0, I10.pin_1
  N65: R11.Pin_0, J9.pin7, C11.0, I11.pin_1
  N66: R12.Pin_0, J9.pin6, C12.0, I12.pin_1
  N67: R13.Pin_0, J9.pin5, C13.0, I13.pin_1
  N68: J2.pin1, J19.pin1
  N69: J2.pin2, J19.pin2
  N70: R14.Pin_0, J9.pin4, C14.0, I14.pin_1
  N71: R15.Pin_0, J9.pin3, C15.0, I15.pin_1
  N72: R16.Pin_0, J9.pin2, C16.0, I16.pin_1
  N73: IC1.COM_-_Common, Q1.pin1, Q2.pin1, Q3.pin1, Q4.pin1, Q5.pin1, Q6.pin1, Q7.pin1, Q8.pin1, J27.pin1, J27.pin2, J27.pin3, J27.pin4, J27.pin5, J27.pin6, JP2.pin2, JP3.pin1
  N74: IC1.Out_8, R24.Pin_1
  N75: IC1.Out_7, R23.Pin_1
  N76: IC1.Out_6, R22.Pin_1
  N77: IC1.Out_5, R21.Pin_1
  N78: IC1.Out_4, R20.Pin_1
  N79: IC1.Out_3, R19.Pin_1
  N80: IC1.Out_2, R18.Pin_1
  N81: IC1.Out_1, R17.Pin_1
  N82: IC2.COM_-_Common, Q16.pin1, Q9.pin1, Q10.pin1, Q11.pin1, Q12.pin1, Q13.pin1, Q14.pin1, Q15.pin1, JP1.pin2, JP3.pin2
  N83: IC2.Out_8, R32.Pin_1
  N84: IC2.Out_7, R31.Pin_1
  N85: IC2.Out_6, R30.Pin_1
  N86: IC2.Out_5, R29.Pin_1
  N87: IC2.Out_4, R28.Pin_1
  N88: IC2.Out_3, R27.Pin_1
  N89: IC2.Out_2, R26.Pin_1
  N90: IC2.Out_1, R25.Pin_1
  N91: R17.Pin_0, Q1.pin2
  N92: R18.Pin_0, Q2.pin2
  N93: R19.Pin_0, Q3.pin2
  N94: R20.Pin_0, Q4.pin2
  N95: R21.Pin_0, Q5.pin2
  N96: R22.Pin_0, Q6.pin2
  N97: R23.Pin_0, Q7.pin2
  N98: R24.Pin_0, Q8.pin2
  N99: R25.Pin_0, Q9.pin2
  N100: R26.Pin_0, Q10.pin2
  N101: R27.Pin_0, Q11.pin2
  N102: R28.Pin_0, Q12.pin2
  N103: R29.Pin_0, Q13.pin2
  N104: R30.Pin_0, Q14.pin2
  N105: R31.Pin_0, Q15.pin2
  N106: R32.Pin_0, Q16.pin2
  N107: JP1.pin3, J22.pin1

notes:
  Vin Ext
  5V
  COMMUNICATION
  PWM
  Vin
  GND
  SCL SDA
  ARDUINO Mega 16I/16O Rev 1
  J.MENARD
  ALIM.
  -   +
  EXT.
